# Fritzing sketch Montaje-programador-UNO (saved by Fritzing 0.9.2b)
breadboards: 1

parts:
  Parte1 = Arduino Uno (Rev3)
  U1 = ESP8266 ESP-01 Upgraded WiFi Module [part_number=ESP8266]
  R1 = Resistor [tolerance=±5% resistance=2k package=THT]
  R2 = Resistor [tolerance=±5% resistance=1k package=THT]
  YwRobot_Power_Supply1 = YwRobot Breadboard Power Supply [part_number=545043]
  R3 = Resistor [tolerance=±5% resistance=10k package=THT]
  R4 = Resistor [tolerance=±5% resistance=10k package=THT]

nets:
  GND: Parte1.GND, Parte1.RESET, U1.GPIO_0, U1.GND, R1.Pin_1, YwRobot_Power_Supply1.GND
  N1: Parte1.D0/RX, R2.Pin_0
  N2: Parte1.D1/TX, U1.TXD
  N3: U1.RXD, R1.Pin_0, R2.Pin_1
  VCC: U1.VCC, YwRobot_Power_Supply1.VCC, R3.Pin_1, R4.Pin_1
  N4: U1.RST/GPIO_16, R4.Pin_0
  N5: U1.CH_PD, R3.Pin_0

custom parts:
  ESP8266 ESP-01 Upgraded WiFi Module: Upgraded Version ESP-01,all Flash are upgraded to 1M byte.Also support Cloud service remote transmission.
  YwRobot Breadboard Power Supply: The YwRobot Breadboard Power Supply (MB-V2) has two power rails; they can be 5V or 3V3. Power to the module can be provided through the female USB socket or through the A10 (female) 2.1mm power jack.
